# Fritzing sketch ESP32_radio (saved by Fritzing 0.9.3b)
breadboards: 1

parts:
  SP2 = SPEAKER [package=pcb_mount_speaker]
  VS1053B2 = VS1053B
  M1 = esp32_p30_w11 [part_number=ESP32S-PIN30]
  AMP1 = GF1002 Stereo Amplifier

nets:
  N1: SP2.+, AMP1.LOUT-
  N2: SP2.-, AMP1.LOUT+
  N3: VS1053B2.XCS, M1.connector20
  N4: VS1053B2.XDCS, M1.connector21
  N5: VS1053B2.DREQ, M1.connector19
  N6: VS1053B2.MOSI, M1.connector14
  N7: VS1053B2.SCK, M1.connector8
  N8: VS1053B2.MISO, M1.connector9
  N9: VS1053B2.XRST, M1.connector15

custom parts:
  VS1053B: VS1053B module
  GF1002 Stereo Amplifier: GF1002 6 Watt Stereo Amplifier
